// Logisim project MIPS.circ as structural Verilog: 1 circuit, main circuit main
module main (
  input  Branch,
  input  RegDst,
  input  ALUSrc,
  input  jump,
  input  RegWrite,
  input  MemWrite,
  input  MemtoReg,
  input  [2:0] ALUControl
);

  wire alu_1_zero, and_1_out, button_1_out, CLK;
  wire [4:0] multiplexer_3_out;
  wire [7:0] adder_1_out, multiplexer_1_out, multiplexer_2_out, PC_q, shifter_1_out;
  wire [19:0] shifter_1_out_2;
  wire [27:0] bit_extender_3_out;
  wire [31:0] adder_2_out, alu_1_alu_result, bit_extender_1_out, bit_extender_2_out, data_mem_1_rd,
       multiplexer_4_out, multiplexer_5_out, regfile32_1_rd1, regfile32_1_rd2, rom_1_data, shifter_2_out;

  Clock clock_1 (.out(CLK));
  // Probe on adder_1_out
  Multiplexer #(.width(8)) multiplexer_1 (
    .in0(adder_1_out), .in1(adder_2_out[7:0]), .out(multiplexer_1_out), .sel(and_1_out));  // open: en
  Button button_1 (.out(button_1_out));
  // Probe on adder_2_out[7:0]
  Multiplexer #(.width(8)) multiplexer_2 (
    .in0(multiplexer_1_out), .in1(shifter_1_out), .out(multiplexer_2_out), .sel(jump));  // open: en
  Register PC (.D(multiplexer_2_out), .Q(PC_q), .clk(CLK), .clr(button_1_out));  // open: en
  Adder adder_1 (.a(PC_q), .b(8'h4), .out(adder_1_out));  // open: cin, cout
  // Probe on rom_1_data[25:21]
  ROM #(.addrWidth(6), .dataWidth(32)) rom_1 (.addr(PC_q[7:2]), .data(rom_1_data));  // open: sel
  assign bit_extender_1_out = {{24{1'b0}}, adder_1_out};  // Bit_Extender bit_extender_1
  RegFile32 regfile32_1 (
    .AD1(rom_1_data[25:21]), .AD2(rom_1_data[20:16]), .CLK(CLK), .WE(RegWrite), .AD3(multiplexer_3_out),
    .WD3(multiplexer_5_out), .RD1(regfile32_1_rd1), .RD2(regfile32_1_rd2));
  assign bit_extender_2_out = {{16{rom_1_data[15]}}, rom_1_data[15:0]};  // Bit_Extender bit_extender_2
  assign bit_extender_3_out = {{2{rom_1_data[25]}}, rom_1_data[25:0]};  // Bit_Extender bit_extender_3
  Multiplexer #(.width(5)) multiplexer_3 (
    .in0(rom_1_data[20:16]), .in1(rom_1_data[15:11]), .out(multiplexer_3_out), .sel(RegDst));  // open: en
  // Probe on bit_extender_2_out
  Shifter #(.width(28)) shifter_1 (.in(bit_extender_3_out), .\dist (5'b00010), .out({shifter_1_out_2, shifter_1_out}));
  Multiplexer #(.width(32)) multiplexer_4 (
    .in0(regfile32_1_rd2), .in1(bit_extender_2_out), .out(multiplexer_4_out), .sel(ALUSrc));  // open: en
  Shifter #(.width(32)) shifter_2 (.in(bit_extender_2_out), .\dist (5'b00010), .out(shifter_2_out));
  ALU alu_1 (
    .SrcA(regfile32_1_rd1), .SrcB(multiplexer_4_out), .ALU_Control(ALUControl), .Zero(alu_1_zero),
    .ALU_Result(alu_1_alu_result));
  // Probe on shifter_2_out
  // Probe on bit_extender_1_out
  Adder #(.width(32)) adder_2 (.a(shifter_2_out), .b(bit_extender_1_out), .out(adder_2_out));  // open: cin, cout
  and and_1 (and_1_out, Branch, alu_1_zero);
  Data_Mem data_mem_1 (.A(alu_1_alu_result), .CLK(CLK), .WE(MemWrite), .WD(regfile32_1_rd2), .RD(data_mem_1_rd));
  Multiplexer #(.width(32)) multiplexer_5 (
    .in0(alu_1_alu_result), .in1(data_mem_1_rd), .out(multiplexer_5_out), .sel(MemtoReg));  // open: en

  // Notes on the sheet:
  //   A AND NOT B : 100
  //   A OR NOT B : 101
  //   AND : 000
  //   OR : 001
  //   + : 010
  //   A - B : 110
  //   SLT : 111
  //   slt t2 t1 t0
  //   lw t0 0x00(zero)
  //   lw t1 0x01(zero
  //   contents of rom_1 (hex, n*v repeats v):
  //   8c080000 8c090001 128502a
endmodule
